# Fritzing sketch hamster_tracker (saved by Fritzing 0.9.2b)
circuit board: 4.39327cm x 4.64727cm
breadboards: 1

parts:
  LED1 = LED - 5mm [color="Red (633nm)" package="5 mm [THT]"]
  U1 = TEMPERATURE-SENSOR [package=to-92]
  R2 = Resistor [tolerance=±5% resistance=220 package=THT]
  R1 = Resistor [tolerance=±5% resistance=220 package=THT]
  Pi1 = Adafruit Pi Cobbler

nets:
  N1: LED1.cathode, U1.ADJ, Pi1.GND
  N2: LED1.anode, R2.Pin_0
  N3: U1.GND, R1.Pin_1, Pi1.#24
  N4: U1.VCC, R1.Pin_0, Pi1.5V0
  N5: R2.Pin_1, Pi1.#4

custom parts:
  Adafruit Pi Cobbler: Adafruit Pi Cobbler GPIO Breakout for Raspberry Pi
